// Logisim project p1.circ as structural Verilog
module NAND1 (
  input  in_1,
  input  in_2,
  output out_3
);

  wire and_1_out;

  and and_1 (and_1_out, in_1, in_2);
  not not_1 (out_3, and_1_out);
endmodule

module NOR1 (
  input  in_1,
  input  in_2,
  output out_3
);

  wire or_1_out;

  or or_1 (or_1_out, in_1, in_2);
  not not_1 (out_3, or_1_out);
endmodule

module XOR1 (
  input  in_1,
  input  in_2,
  output out_3
);

  wire and_1_out, and_2_out, not_1_out, not_2_out;

  not not_1 (not_1_out, in_1);
  not not_2 (not_2_out, in_2);
  and and_1 (and_1_out, in_2, not_1_out);
  and and_2 (and_2_out, not_2_out, in_1);
  or or_1 (out_3, and_1_out, and_2_out);
endmodule

module MUX21 (
  input  in_1,
  input  in_2,
  input  in_3,
  output out_4
);

  wire nand1_1_out_3, nand1_2_out_3, nand1_3_out_3;

  NAND1 nand1_1 (.in_1(in_2), .in_2(in_2), .out_3(nand1_1_out_3));
  NAND1 nand1_2 (.in_1(in_1), .in_2(in_2), .out_3(nand1_2_out_3));
  NAND1 nand1_3 (.in_1(nand1_1_out_3), .in_2(in_3), .out_3(nand1_3_out_3));
  NAND1 nand1_4 (.in_1(nand1_2_out_3), .in_2(nand1_3_out_3), .out_3(out_4));
endmodule

module MUX41 (
  input  in_1,
  input  in_2,
  input  in_3,
  input  in_4,
  input  in_5,
  input  in_6,
  output out_7
);

  wire mux21_1_out_4, mux21_2_out_4;

  MUX21 mux21_1 (.in_1(in_1), .in_2(in_4), .in_3(in_2), .out_4(mux21_1_out_4));
  MUX21 mux21_2 (.in_1(in_5), .in_2(in_4), .in_3(in_6), .out_4(mux21_2_out_4));
  MUX21 mux21_3 (.in_1(mux21_1_out_4), .in_2(in_3), .in_3(mux21_2_out_4), .out_4(out_7));
endmodule
