// Logisim project p4.circ as structural Verilog
module Ex4 (
  input  [7:0] Input1,
  output Out1,
  output [7:0] Out2
);

  and and_1 (Out1, Input1[0], Input1[7]);
  not not_1 (Out2[7], Input1[7]);

  assign Out2[6:0] = Input1[6:0];
endmodule
