// Logisim project p5.circ as structural Verilog
module rotr (
  input  [15:0] A,
  input  [3:0] B,
  output [15:0] out_3
);

  wire [15:0] rotate1_1_out_3, rotate2_1_out_3, rotate4_1_out_3;

  rotate1 rotate1_1 (.in_1(A), .in_2(B[0]), .out_3(rotate1_1_out_3));
  rotate2 rotate2_1 (.in_1(rotate1_1_out_3), .in_2(B[1]), .out_3(rotate2_1_out_3));
  rotate4 rotate4_1 (.in_1(rotate2_1_out_3), .in_2(B[2]), .out_3(rotate4_1_out_3));
  rotate8 rotate8_1 (.in_1(rotate4_1_out_3), .in_2(B[3]), .out_3(out_3));
endmodule

module rotate1 (
  input  [15:0] in_1,
  input  in_2,
  output [15:0] out_3
);

  wire not_1_out;

  Multiplexer #(.width(16), .enable("false")) multiplexer_1 (
    .in0({in_1[0], in_1[15:1]}), .in1(in_1), .out(out_3), .sel(not_1_out));
  not not_1 (not_1_out, in_2);
endmodule

module rotate2 (
  input  [15:0] in_1,
  input  in_2,
  output [15:0] out_3
);

  wire [15:0] rotate1_1_out_3;

  rotate1 rotate1_1 (.in_1(in_1), .in_2(in_2), .out_3(rotate1_1_out_3));
  rotate1 rotate1_2 (.in_1(rotate1_1_out_3), .in_2(in_2), .out_3(out_3));
endmodule

module rotate4 (
  input  [15:0] in_1,
  input  in_2,
  output [15:0] out_3
);

  wire [15:0] rotate2_1_out_3;

  rotate2 rotate2_1 (.in_1(in_1), .in_2(in_2), .out_3(rotate2_1_out_3));
  rotate2 rotate2_2 (.in_1(rotate2_1_out_3), .in_2(in_2), .out_3(out_3));
endmodule

module rotate8 (
  input  [15:0] in_1,
  input  in_2,
  output [15:0] out_3
);

  wire [15:0] rotate4_1_out_3;

  rotate4 rotate4_1 (.in_1(in_1), .in_2(in_2), .out_3(rotate4_1_out_3));
  rotate4 rotate4_2 (.in_1(rotate4_1_out_3), .in_2(in_2), .out_3(out_3));
endmodule
