// Logisim project cpu.circ as structural Verilog: 8 circuits, main circuit main
module main (
  input  [31:0] INSTRUCTION,
  input  CLOCK,
  output [31:0] FETCH_ADDRESS,
  output [31:0] ra,
  output [31:0] sp,
  output [31:0] t0,
  output [31:0] t1,
  output [31:0] t2,
  output [31:0] s0,
  output [31:0] s1,
  output [31:0] a0
);

  wire asel, breq, brlt, brun, bsel, memrw, nop, pcsel, write_en;
  wire [1:0] wbsel;
  wire [2:0] funct3, immsel;
  wire [3:0] alusel;
  wire [4:0] A_reg, B_reg, imm7_31;
  wire [6:0] funct7, opcode;
  wire [31:0] A, adder_1_out, alu_out, B, dmem_out, immediate, multiplexer_1_out, multiplexer_2_out,
       multiplexer_3_out, multiplexer_4_out, pc_out, pc_plus_4, PROGRAM_COUNTER, wb;

  Shifter #(.width(32), .shift("lr")) shifter_1 (.in(PROGRAM_COUNTER), .\dist (5'b00010), .out(FETCH_ADDRESS));
  Adder #(.width(32)) adder_1 (.a(PROGRAM_COUNTER), .b(32'h4), .out(adder_1_out));  // open: cin, cout
  Multiplexer #(.width(32), .enable("false")) multiplexer_1 (
    .in0(adder_1_out), .in1(alu_out), .out(multiplexer_1_out), .sel(pcsel));
  Register #(.width(32)) register_1 (.D(PROGRAM_COUNTER), .clk(CLOCK), .Q(pc_out));  // open: en, clr
  Register #(.width(32)) register_2 (.D(multiplexer_1_out), .clk(CLOCK), .Q(PROGRAM_COUNTER));  // open: en, clr
  Register #(.width(32)) register_3 (
    .D(multiplexer_2_out), .clk(CLOCK), .Q({funct7, B_reg, A_reg, funct3, imm7_31, opcode}));  // open: en, clr
  Multiplexer #(.width(32), .enable("false")) multiplexer_2 (
    .in0(INSTRUCTION), .in1(32'h13), .out(multiplexer_2_out), .sel(nop));
  Adder #(.width(32)) adder_2 (.a(pc_out), .b(32'h4), .out(pc_plus_4));  // open: cin, cout
  imm_gen imm_gen_1 (
    .immediate_instruction({funct7, B_reg, A_reg, funct3, imm7_31}), .immediate_select(immsel),
    .out_3(immediate));
  regfile_main main_1 (
    .rs2(B_reg), .rd(imm7_31), .Read_Data_1(A), .Read_Data_2(B), .ra(ra), .sp(sp), .t0(t0), .t1(t1), .t2(t2),
    .s0(s0), .s1(s1), .a0(a0), .rs1(A_reg), .Write_Data(wb), .RegWEn(write_en), .clk(CLOCK));
  Multiplexer #(.width(32), .enable("false")) multiplexer_3 (
    .in0(A), .in1(pc_out), .out(multiplexer_3_out), .sel(asel));
  Multiplexer #(.width(32), .enable("false")) multiplexer_4 (
    .in0(B), .in1(immediate), .out(multiplexer_4_out), .sel(bsel));
  control_logic control_logic_1 (
    .in_1(breq), .in_2(brlt), .in_3(opcode), .in_4(funct3), .in_5(funct7), .out_6(pcsel), .out_7(nop),
    .out_8(write_en), .out_9(immsel), .out_10(asel), .out_11(bsel), .out_12(alusel), .out_13(brun),
    .out_14(memrw), .out_15(wbsel));
  branch_comparator branch_comparator_1 (.A(A), .B(B), .br_un(brun), .br_eq(breq), .br_lt(brlt));
  mem_main main_2 (.Address(alu_out), .Write_Data(B), .Write_En(memrw), .Read_Data(dmem_out), .clk(CLOCK));
  Multiplexer #(.select(2), .width(32), .enable("false")) multiplexer_5 (
    .in0(alu_out), .in1(pc_plus_4), .in2(dmem_out), .out(wb), .sel(wbsel));  // open: in3
  alu alu_1 (.A(multiplexer_3_out), .B(multiplexer_4_out), .ALUSel(alusel), .Result(alu_out));

  // Other names for the same wires on the sheet: read_register[4:0] = imm7_31;
  //   imm7_31[24:5] = {funct7, B_reg, A_reg, funct3}; clk = CLOCK

  // Notes on the sheet:
  //   Output
  //   Inputs/Outputs from run.circ. DO NOT MOVE THESE.
  //   Inputs
  //   STEP 1; INSTRUCTION FETCHING
  //   STEP 2; INSTRUCTION DECODING
  //   STEP 3; EXECUTE
  //   STEP 4; MEMORY
  //   STEP 5; WRITE BACK
  //   Inputs/Outputs from run.circ. DO NOT MOVE THESE.
endmodule

module branch_comparator (
  input  [31:0] A,
  input  [31:0] B,
  input  br_un,
  output br_eq,
  output br_lt
);

  wire beqs, bequ, blts, bltu;

  Comparator #(.width(32)) comparator_1 (.a(A), .b(B), .eq(beqs), .lt(blts));  // open: gt
  Multiplexer #(.enable("false")) multiplexer_1 (.in0(beqs), .in1(bequ), .out(br_eq), .sel(br_un));
  Comparator #(.width(32), .mode("unsigned")) comparator_2 (.a(A), .b(B), .eq(bequ), .lt(bltu));  // open: gt
  Multiplexer #(.enable("false")) multiplexer_2 (.in0(blts), .in1(bltu), .out(br_lt), .sel(br_un));

  // Other names for the same wires on the sheet: brun = br_un

  // Notes on the sheet:
  //   Inputs
  //   Work
  //   Outputs
endmodule

module imm_gen (
  input  [24:0] immediate_instruction,
  input  [2:0] immediate_select,
  output [31:0] out_3
);

  wire [31:0] b_type, i_type, j_type, r_type, s_type;

  assign i_type = {{20{immediate_instruction[24]}}, immediate_instruction[24:13]};  // Bit_Extender bit_extender_1
  assign s_type = {{20{immediate_instruction[24]}}, {immediate_instruction[24:18], immediate_instruction[4:0]}};  // Bit_Extender bit_extender_2
  Multiplexer #(.select(3), .width(32), .enable("false")) multiplexer_1 (
    .in0(i_type), .in1(s_type), .in2(b_type), .in3({immediate_instruction[24:5], {12{1'b0}}}), .in4(j_type),
    .in5(r_type), .out(out_3), .sel(immediate_select));  // open: in6, in7
  assign j_type = {{11{immediate_instruction[24]}}, {immediate_instruction[24], immediate_instruction[12:5], immediate_instruction[13], immediate_instruction[23:14], 1'b0}};  // Bit_Extender bit_extender_3
  assign b_type = {{19{immediate_instruction[24]}}, {immediate_instruction[24], immediate_instruction[0], immediate_instruction[23:18], immediate_instruction[4:1], 1'b0}};  // Bit_Extender bit_extender_4
  assign r_type = {{25{immediate_instruction[24]}}, immediate_instruction[24:18]};  // Bit_Extender bit_extender_5

  // Other names for the same wires on the sheet: instruction[24:0] = immediate_instruction;
  //   u_type[31:12] = immediate_instruction[24:5]; immsel[2:0] = immediate_select

  // Notes on the sheet:
  //   Determining Immediate by Instruction Type
  //   Selecting Relevant Immediate
  //   Inputs
  //   32-Bit Immediate
endmodule

module control_logic (
  input  in_1,
  input  in_2,
  input  [6:0] in_3,
  input  [2:0] in_4,
  input  [6:0] in_5,
  output out_6,
  output out_7,
  output out_8,
  output [2:0] out_9,
  output out_10,
  output out_11,
  output [3:0] out_12,
  output out_13,
  output out_14,
  output [1:0] out_15
);

  wire add, addi, and_20_out, and_21_out, and_22_out, and_23_out, and_fb972c03, andi, B, beq, blt, bne,
       comparator_1_eq, comparator_2_eq, comparator_3_eq, comparator_4_eq, comparator_5_eq, comparator_6_eq,
       comparator_7_eq, comparator_8_eq, comparator_9_eq, comparator_10_eq, comparator_11_eq,
       comparator_12_eq, comparator_13_eq, comparator_14_eq, comparator_15_eq, comparator_16_eq,
       comparator_17_eq, comparator_18_eq, comparator_19_eq, comparator_20_eq, comparator_21_eq,
       comparator_22_eq, comparator_23_eq, comparator_24_eq, comparator_25_eq, comparator_26_eq,
       comparator_27_eq, comparator_28_eq, comparator_29_eq, comparator_30_eq, comparator_31_eq,
       comparator_32_eq, comparator_33_eq, comparator_34_eq, comparator_35_eq, comparator_36_eq,
       comparator_37_eq, comparator_38_eq, comparator_39_eq, comparator_40_eq, comparator_41_eq,
       comparator_42_eq, comparator_43_eq, comparator_44_eq, comparator_45_eq, comparator_46_eq,
       comparator_47_eq, comparator_48_eq, comparator_49_eq, divu, I, imm1, imm2, imm3, imm4, J, jalr, lb,
       lh, lui, lw, lwc, mul, mulh, mulhu, not_2_out, or_e577c5a5, ori, pop, push, R, remu, sll_a3555964,
       slli, slt, slti, sra_1149deca, srai, srl_a1fe72ac, srli, sub, sw, xor_8a11d922, xori;

  or or_1 (out_15[0], J, jalr);
  or or_2 (out_15[1], lw, lh, lb);
  immselectsub immselectsub_1 (
    .in_1(out_14), .in_2(lwc), .in_3(lui), .in_4(B), .in_5(lui), .in_6(lwc), .in_7(J), .out_8(out_9));
  or or_3 (out_12[0], and_fb972c03, andi, xor_8a11d922, xori, sra_1149deca, srai, slt, slti, remu, mulhu);
  or or_4 (out_12[1], or_e577c5a5, ori, xor_8a11d922, xori, sll_a3555964, slli, slt, slti, mul, mulhu, mulh);
  or or_5 (out_12[2], srl_a1fe72ac, srli, sra_1149deca, srai, sll_a3555964, slli, slt, sub, mulh);
  or or_6 (out_8, R, I, lui, J);
  or or_7 (out_12[3], divu, remu, mul, mulhu, sub, mulh);
  or or_8 (out_10, J, B);
  not not_1 (out_11, R);
  Comparator #(.width(3)) comparator_1 (.a(in_4), .b(3'b000), .eq(comparator_1_eq));  // open: gt, lt
  Comparator #(.width(3)) comparator_2 (.a(in_4), .b(3'b110), .eq(comparator_2_eq));  // open: gt, lt
  Comparator #(.width(3)) comparator_3 (.a(in_4), .b(3'b010), .eq(comparator_3_eq));  // open: gt, lt
  Comparator #(.width(3)) comparator_4 (.a(in_4), .b(3'b001), .eq(comparator_4_eq));  // open: gt, lt
  Comparator #(.width(3)) comparator_5 (.a(in_4), .b(3'b001), .eq(comparator_5_eq));  // open: gt, lt
  Comparator #(.width(3)) comparator_6 (.a(in_4), .b(3'b100), .eq(comparator_6_eq));  // open: gt, lt
  Comparator #(.width(3)) comparator_7 (.a(in_4), .b(3'b110), .eq(comparator_7_eq));  // open: gt, lt
  Comparator #(.width(7)) comparator_8 (.a(in_5), .b({7{1'b0}}), .eq(comparator_8_eq));  // open: gt, lt
  Comparator #(.width(7)) comparator_9 (.a(in_5), .b({7{1'b0}}), .eq(comparator_9_eq));  // open: gt, lt
  Comparator #(.width(7)) comparator_10 (.a(in_5), .b({7{1'b0}}), .eq(comparator_10_eq));  // open: gt, lt
  Comparator #(.width(3)) comparator_11 (.a(in_4), .b(3'b000), .eq(comparator_11_eq));  // open: gt, lt
  Comparator #(.width(3)) comparator_12 (.a(in_4), .b(3'b010), .eq(comparator_12_eq));  // open: gt, lt
  and and_1 (sw, comparator_12_eq, out_14);
  btype btype_1 (.funct_3(in_4), .b_val(B), .out_beq(beq), .out_blt(blt), .out_bltu(out_13), .outbne(bne));
  and and_2 (addi, comparator_1_eq, imm2);
  and and_3 (ori, comparator_2_eq, imm2);
  and and_4 (slti, comparator_3_eq, imm2);
  and and_5 (lh, comparator_4_eq, imm1);
  and and_6 (sll_a3555964, comparator_8_eq, comparator_5_eq, R);
  and and_7 (xor_8a11d922, comparator_9_eq, comparator_6_eq, R);
  and and_8 (or_e577c5a5, comparator_10_eq, comparator_7_eq, R);
  Comparator #(.width(7)) comparator_13 (.a(in_5), .b(7'b0000001), .eq(comparator_13_eq));  // open: gt, lt
  Comparator #(.width(3)) comparator_14 (.a(in_4), .b(3'b101), .eq(comparator_14_eq));  // open: gt, lt
  Comparator #(.width(7)) comparator_15 (.a(in_5), .b(7'b0100000), .eq(comparator_15_eq));  // open: gt, lt
  and and_9 (divu, comparator_13_eq, comparator_14_eq, R);
  and and_10 (sub, comparator_15_eq, comparator_11_eq, R);
  instructiontype instructiontype_1 (
    .opcode_in(in_3), .funct_3(in_4), .i1(imm1), .i2(imm2), .i3(imm3), .i4(imm4), .i(I), .r(R), .u(lui),
    .j(J), .s(out_14), .b(B));
  Comparator #(.width(3)) comparator_16 (.a(in_4), .b(3'b101), .eq(comparator_16_eq));  // open: gt, lt
  Comparator #(.width(3)) comparator_17 (.a(in_4), .b(3'b101), .eq(comparator_17_eq));  // open: gt, lt
  Comparator #(.width(3)) comparator_18 (.a(in_4), .b(3'b000), .eq(comparator_18_eq));  // open: gt, lt
  Comparator #(.width(3)) comparator_19 (.a(in_4), .b(3'b100), .eq(comparator_19_eq));  // open: gt, lt
  Comparator #(.width(7)) comparator_20 (.a(in_5), .b({7{1'b0}}), .eq(comparator_20_eq));  // open: gt, lt
  and and_11 (srli, comparator_20_eq, comparator_16_eq, imm2);
  Comparator #(.width(7)) comparator_21 (.a(in_5), .b(7'b0100000), .eq(comparator_21_eq));  // open: gt, lt
  and and_12 (lb, comparator_18_eq, imm1);
  and and_13 (xori, comparator_19_eq, imm2);
  and and_14 (srai, comparator_21_eq, comparator_17_eq, imm2);
  Comparator #(.width(3)) comparator_22 (.a(in_4), .b(3'b010), .eq(comparator_22_eq));  // open: gt, lt
  Comparator #(.width(3)) comparator_23 (.a(in_4), .b(3'b101), .eq(comparator_23_eq));  // open: gt, lt
  Comparator #(.width(7)) comparator_24 (.a(in_5), .b(7'b0100000), .eq(comparator_24_eq));  // open: gt, lt
  Comparator #(.width(3)) comparator_25 (.a(in_4), .b(3'b101), .eq(comparator_25_eq));  // open: gt, lt
  Comparator #(.width(3)) comparator_26 (.a(in_4), .b(3'b000), .eq(comparator_26_eq));  // open: gt, lt
  Comparator #(.width(3)) comparator_27 (.a(in_4), .b(3'b000), .eq(comparator_27_eq));  // open: gt, lt
  and and_15 (slt, comparator_28_eq, comparator_22_eq, R);
  Comparator #(.width(7)) comparator_28 (.a(in_5), .b({7{1'b0}}), .eq(comparator_28_eq));  // open: gt, lt
  Comparator #(.width(7)) comparator_29 (.a(in_5), .b({7{1'b0}}), .eq(comparator_29_eq));  // open: gt, lt
  and and_16 (sra_1149deca, comparator_24_eq, comparator_25_eq, R);
  Comparator #(.width(7)) comparator_30 (.a(in_5), .b(7'b0000001), .eq(comparator_30_eq));  // open: gt, lt
  Comparator #(.width(7)) comparator_31 (.a(in_5), .b({7{1'b0}}), .eq(comparator_31_eq));  // open: gt, lt
  and and_17 (srl_a1fe72ac, comparator_29_eq, comparator_23_eq, R);
  and and_18 (mul, comparator_30_eq, comparator_26_eq, R);
  and and_19 (add, comparator_31_eq, comparator_27_eq, R);
  immtype immtype_1 (.opcode_in(in_3), .funct_3(in_4), .i1(imm1), .i2(imm2), .i3(imm3), .i4(imm4));
  Comparator #(.width(3)) comparator_32 (.a(in_4), .b(3'b010), .eq(comparator_32_eq));  // open: gt, lt
  Comparator #(.width(3)) comparator_33 (.a(in_4), .b(3'b000), .eq(comparator_33_eq));  // open: gt, lt
  and and_20 (and_20_out, beq, in_1);
  and and_21 (and_21_out, bne, not_2_out);
  not not_2 (not_2_out, in_1);
  and and_22 (and_22_out, blt, in_2);
  and and_23 (and_23_out, out_13, in_2);
  and and_24 (lw, comparator_32_eq, imm1);
  and and_25 (jalr, comparator_33_eq, imm3);
  Comparator #(.width(3)) comparator_34 (.a(in_4), .b(3'b111), .eq(comparator_34_eq));  // open: gt, lt
  Comparator #(.width(3)) comparator_35 (.a(in_4), .b(3'b111), .eq(comparator_35_eq));  // open: gt, lt
  Comparator #(.width(3)) comparator_36 (.a(in_4), .b(3'b001), .eq(comparator_36_eq));  // open: gt, lt
  Comparator #(.width(3)) comparator_37 (.a(in_4), .b(3'b011), .eq(comparator_37_eq));  // open: gt, lt
  or or_9 (out_6, J, and_20_out, and_21_out, and_22_out, and_23_out, jalr);
  Comparator #(.width(3)) comparator_38 (.a(in_4), .b(3'b010), .eq(comparator_38_eq));  // open: gt, lt
  Comparator #(.width(7)) comparator_39 (.a(in_3), .b(7'b0111011), .eq(comparator_39_eq));  // open: gt, lt
  Comparator #(.width(3)) comparator_40 (.a(in_4), .b(3'b111), .eq(comparator_40_eq));  // open: gt, lt
  Comparator #(.width(3)) comparator_41 (.a(in_4), .b(3'b001), .eq(comparator_41_eq));  // open: gt, lt
  Comparator #(.width(7)) comparator_42 (.a(in_5), .b(7'b0000001), .eq(comparator_42_eq));  // open: gt, lt
  Comparator #(.width(7)) comparator_43 (.a(in_5), .b({7{1'b0}}), .eq(comparator_43_eq));  // open: gt, lt
  Comparator #(.width(3)) comparator_44 (.a(in_4), .b(3'b111), .eq(comparator_44_eq));  // open: gt, lt
  Comparator #(.width(3)) comparator_45 (.a(in_4), .b(3'b011), .eq(comparator_45_eq));  // open: gt, lt
  Comparator #(.width(7)) comparator_46 (.a(in_3), .b(7'b0111011), .eq(comparator_46_eq));  // open: gt, lt
  and and_26 (mulh, comparator_47_eq, comparator_36_eq, R);
  Comparator #(.width(7)) comparator_47 (.a(in_5), .b(7'b0000001), .eq(comparator_47_eq));  // open: gt, lt
  Comparator #(.width(7)) comparator_48 (.a(in_5), .b(7'b0000001), .eq(comparator_48_eq));  // open: gt, lt
  and and_27 (mulhu, comparator_48_eq, comparator_37_eq, R);
  and and_28 (pop, comparator_38_eq, comparator_39_eq);
  Comparator #(.width(7)) comparator_49 (.a(in_5), .b({7{1'b0}}), .eq(comparator_49_eq));  // open: gt, lt
  and and_29 (remu, comparator_42_eq, comparator_34_eq, R);
  and and_30 (and_fb972c03, comparator_43_eq, comparator_35_eq, R);
  and and_31 (lwc, comparator_44_eq, imm1);
  and and_32 (push, comparator_45_eq, comparator_46_eq);
  and and_33 (andi, comparator_40_eq, imm2);
  and and_34 (slli, comparator_49_eq, comparator_41_eq, imm2);

  assign out_7 = out_6;

  // Other names for the same wires on the sheet: ALUSel[3:0] = out_12; bltu = out_13; br_eq = in_1; br_lt = in_2;
  //   funct3[2:0] = in_4; funct7[6:0] = in_5; immsel[2:0] = out_9; jal = J; U = lui; opcode[6:0] = in_3;
  //   pcsel = out_6; S = out_14; WBSel[1:0] = out_15

  // Notes on the sheet:
  //   Control Inputs
  //   Writeback Select
  //   Immediate Select
  //   ALU Select
  //   Control Outputs
  //   S-Type Instructions
  //   B-Type Instructions
  //   I-Type Instructions
  //   R-Type Instructions
  //   Determine Instruction Type
  //   U-Type Instructions
  //   J-Type Instructions
  //   Immediate Type
  //   Program Counter (PC) Select
endmodule

module immselectsub (
  input  in_1,
  input  in_2,
  input  in_3,
  input  in_4,
  input  in_5,
  input  in_6,
  input  in_7,
  output [2:0] out_8
);

  or or_1 (out_8[0], in_1, in_2, in_3);
  or or_2 (out_8[1], in_4, in_5);
  or or_3 (out_8[2], in_6, in_7);
endmodule

module btype (
  input  [2:0] funct_3,
  input  b_val,
  output out_beq,
  output out_blt,
  output out_bltu,
  output outbne
);

  wire comparator_1_eq, comparator_2_eq, comparator_3_eq, comparator_4_eq;

  Comparator #(.width(3)) comparator_1 (.a(funct_3), .b(3'b100), .eq(comparator_1_eq));  // open: gt, lt
  Comparator #(.width(3)) comparator_2 (.a(funct_3), .b(3'b000), .eq(comparator_2_eq));  // open: gt, lt
  and and_1 (out_beq, comparator_2_eq, b_val);
  and and_2 (out_blt, comparator_1_eq, b_val);
  Comparator #(.width(3)) comparator_3 (.a(funct_3), .b(3'b110), .eq(comparator_3_eq));  // open: gt, lt
  Comparator #(.width(3)) comparator_4 (.a(funct_3), .b(3'b001), .eq(comparator_4_eq));  // open: gt, lt
  and and_3 (out_bltu, comparator_3_eq, b_val);
  and and_4 (outbne, comparator_4_eq, b_val);

  // Other names for the same wires on the sheet: B = b_val; beq = out_beq; blt = out_blt; bltu = out_bltu;
  //   bne = outbne; funct3[2:0] = funct_3
endmodule

module instructiontype (
  input  [6:0] opcode_in,
  input  [2:0] funct_3,
  input  i1,
  input  i2,
  input  i3,
  input  i4,
  output i,
  output r,
  output u,
  output j,
  output s,
  output b
);

  wire and_1_out, comparator_1_eq, comparator_2_eq, comparator_3_eq;

  Comparator #(.width(7)) comparator_1 (.a(opcode_in), .b(7'b0110011), .eq(comparator_1_eq));  // open: gt, lt
  Comparator #(.width(7)) comparator_2 (.a(opcode_in), .b(7'b0111011), .eq(comparator_2_eq));  // open: gt, lt
  Comparator #(.width(3)) comparator_3 (.a(funct_3), .b(3'b011), .eq(comparator_3_eq));  // open: gt, lt
  or or_1 (r, comparator_1_eq, and_1_out);
  and and_1 (and_1_out, comparator_2_eq, comparator_3_eq);
  or or_2 (i, i1, i2, i3, i4);
  Comparator #(.width(7)) comparator_4 (.a(opcode_in), .b(7'b0110111), .eq(u));  // open: gt, lt
  Comparator #(.width(7)) comparator_5 (.a(opcode_in), .b(7'b1101111), .eq(j));  // open: gt, lt
  Comparator #(.width(7)) comparator_6 (.a(opcode_in), .b(7'b0100011), .eq(s));  // open: gt, lt
  Comparator #(.width(7)) comparator_7 (.a(opcode_in), .b(7'b1100011), .eq(b));  // open: gt, lt

  // Other names for the same wires on the sheet: funct3[2:0] = funct_3; imm1 = i1; imm2 = i2; imm3 = i3; imm4 = i4;
  //   opcode[6:0] = opcode_in
endmodule

module immtype (
  input  [6:0] opcode_in,
  input  [2:0] funct_3,
  output i1,
  output i2,
  output i3,
  output i4
);

  wire comparator_2_eq, comparator_3_eq;

  Comparator #(.width(7)) comparator_1 (.a(opcode_in), .b(7'b0010011), .eq(i2));  // open: gt, lt
  Comparator #(.width(3)) comparator_2 (.a(funct_3), .b(3'b010), .eq(comparator_2_eq));  // open: gt, lt
  Comparator #(.width(7)) comparator_3 (.a(opcode_in), .b(7'b0111011), .eq(comparator_3_eq));  // open: gt, lt
  Comparator #(.width(7)) comparator_4 (.a(opcode_in), .b(7'b0000011), .eq(i1));  // open: gt, lt
  Comparator #(.width(7)) comparator_5 (.a(opcode_in), .b(7'b1100111), .eq(i3));  // open: gt, lt
  and and_1 (i4, comparator_2_eq, comparator_3_eq);

  // Other names for the same wires on the sheet: funct3[2:0] = funct_3; imm1 = i1; imm2 = i2; imm3 = i3; imm4 = i4;
  //   opcode[6:0] = opcode_in
endmodule
